# Fritzing sketch Circuit (saved by Fritzing 0.9.3b)
breadboards: 1

parts:
  hc-sr1 = hc-sr04
  IC1 = L293D [package=THT]
  M2 = DC Motor
  LED1 = smd LED [color="Red (633nm)" package="0805 [SMD]"]
  M3 = DC Motor
  BAT1 = BC9VPC [package=bc9vpc]
  J1 = Basic Servo
  Part2 = Arduino Micro (Rev3)  # not connected
  IC2 = L293D [package=THT]
  BAT2 = BC9VPC [package=bc9vpc]

nets:
  VCC: hc-sr1.VCC, IC1.+V, J1.vcc, IC2.+V
  GND: hc-sr1.GND, IC1.0V, BAT1.V-, J1.gnd, IC2.0V, BAT2.V-
  N1: IC1.Enable_1, IC2.Enable_1
  N2: IC1.In_1, IC2.In_1
  N3: IC1.Out_1_(_Controlled_by_Enable_1_), LED1.cathode, M3.pin_1, IC2.Out_1_(_Controlled_by_Enable_1_)
  N4: IC1.Out_2_(_Controlled_by_Enable_1_), LED1.anode, M3.pin_2, IC2.Out_2_(_Controlled_by_Enable_1_)
  N5: IC1.In_2, IC2.In_2
  N6: IC1.+Vmotor, BAT1.V+, IC2.+Vmotor
  N7: IC1.Enable_2, IC2.Enable_2
  N8: IC1.In_3, IC2.In_3
  N9: IC1.Out_3_(_Controlled_by_Enable_2_), M2.pin_2, IC2.Out_3_(_Controlled_by_Enable_2_)
  N10: IC1.Out_4_(_Controlled_by_Enable_2_), M2.pin_1, IC2.Out_4_(_Controlled_by_Enable_2_)
  N11: IC1.In_4, IC2.In_4
